# Fritzing sketch devboard (saved by Fritzing 0.9.3b)

parts:
  4_8V = 4 x AAA Battery Mount
  U1 = NodeMCU V3.0
  Part1 = InvenSense MPU6050

nets:
  GND: 4_8V.-, U1.GND, Part1.GND
  VIN: 4_8V.+, U1.Vin, Part1.VCC
  N1: U1.D1, Part1.SCL
  N2: U1.D2, Part1.SDA

custom parts:
  NodeMCU V3.0: ESP8266 based NodeMCU
