# Fritzing sketch schematic (saved by Fritzing 0.9.3b)

parts:
  WeMos_D1_Mini1 = WeMos D1 Mini
  Part1 = InvenSense MPU6050
  4_8V = 4 x AAA Battery Mount

nets:
  5V: WeMos_D1_Mini1.5V, Part1.VCC, 4_8V.+
  N1: WeMos_D1_Mini1.D1, Part1.SCL
  N2: WeMos_D1_Mini1.D2, Part1.SDA
  N3: WeMos_D1_Mini1.G, Part1.GND, 4_8V.-
