# Fritzing sketch schematic (saved by Fritzing 0.9.4)

parts:
  Mod1 = Raspberry Pi 4B
  Part1 = BME280 Breakout

nets:
  3V3: Mod1.3V3, Part1.VCC
  N1: Mod1.GPIO9, Part1.SDA
  N2: Mod1.GPIO11, Part1.SCL
  GND: Mod1.GND, Part1.GND

custom parts:
  BME280 Breakout: SparkFun Atmospheric Sensor Breakout - BME280 SEN-13676 The SparkFun BME280 Atmospheric Sensor Breakout is the easy way to measure barometric pressure, humidity, and temperature readings all without taking up too much space. Basically, anything you need to know about atmospheric conditions you can find out from this tiny breakout. The BME280 Breakout has been design to be used in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
